# Fritzing sketch prototype (saved by Fritzing 0.9.2b)
breadboards: 1

parts:
  Bauteil1 = Arduino Uno (Rev3)
  D2 = Rectifier Diode [part_number=1N4001 package="300 mil [THT]"]
  L2 = Solenoid
  R4 = Resistor [tolerance=±5% resistance=10k package=THT]
  M1 = DC Motor
  Q3 = Basic FET N-Channel [package="TO220 [THT]"]
  R5 = Resistor [tolerance=±5% resistance=680 package=THT]
  R6 = Resistor [tolerance=±5% resistance=10k package=THT]
  D3 = Rectifier Diode [part_number=1N4001 package="300 mil [THT]"]
  U1 = PCF8574 [package="DIP16 [THT]"]
  R7 = Resistor [tolerance=±5% resistance=15k package=THT]
  R8 = Resistor [tolerance=±5% resistance=15k package=THT]
  RHT1 = Humidity and Temperature Sensor RHT03
  Q2 = Basic FET N-Channel [package="TO220 [THT]"]
  C4 = Ceramic Capacitor [capacitance=100nF package="100 mil [THT, multilayer]"]
  Q4 = MOSFET-NCHANNEL [package=to-92]
  R10 = Resistor [tolerance=±5% resistance=2.2k package=THT]
  R11 = Resistor [tolerance=±5% resistance=10k package=THT]

nets:
  GND: Bauteil1.GND, R4.Pin_0, Q3.source, R6.Pin_0, U1.A0, U1.A1, U1.A3, U1.GND, Q2.source, C4.0
  N1: Bauteil1.A4/SDA, U1.SDA, R7.Pin_1, RHT1.GND_1
  N2: Bauteil1.A5/SCL, U1.SCL, R8.Pin_1, RHT1.Data-signal
  N3: Bauteil1.D2, R5.Pin_0, R6.Pin_1
  VCC: Bauteil1.5V, U1.VCC, R7.Pin_0, R8.Pin_0, RHT1.Vcc, C4.1, Q4.G, R11.Pin_0
  N4: Bauteil1.VIN, D2.cathode, L2.pin2, M1.pin_2, D3.cathode
  N5: D2.anode, L2.pin1, Q2.drain
  N6: R4.Pin_1, Q2.gate, Q4.D
  N7: M1.pin_1, Q3.drain, D3.anode
  N8: Q3.gate, R5.Pin_1
  N9: U1.P0, R10.Pin_1
  N10: U1.P1, RHT1.GND_2
  N11: Q4.S, R10.Pin_0, R11.Pin_1
